# Fritzing sketch air_throttle (saved by Fritzing 0.9.3b)
breadboards: 1

parts:
  MOTOR1 = 28BYJ-48 Stepper Motor
  BREAKOUT1 = ULN2003A breakout board
  Pro_Micro1 = SparkFun Pro Micro
  Part1 = ACS712 Low Current Sensor Board v12

nets:
  N1: MOTOR1.RED, BREAKOUT1.BLUE_wire
  N2: MOTOR1.ORANGE, BREAKOUT1.PINK_wire
  N3: MOTOR1.YELLOW, BREAKOUT1.YELLOW_wire
  N4: MOTOR1.PINK, BREAKOUT1.ORANGE_wire
  N5: MOTOR1.BLUE, BREAKOUT1.RED_wire
  N6: BREAKOUT1.In_1, Pro_Micro1.6
  N7: BREAKOUT1.In_2, Pro_Micro1.7
  N8: BREAKOUT1.In_3, Pro_Micro1.8
  N9: BREAKOUT1.In_4, Pro_Micro1.9
  GND: BREAKOUT1.0V, Pro_Micro1.GND, Part1.GND
  +5V: BREAKOUT1.+5V, Pro_Micro1.VCC, Part1.5V
  N10: Pro_Micro1.A0, Part1.VO

notes:
  5V supply
  +
  -
  ACS712 20A

custom parts:
  ULN2003A breakout board: ULN2003A 7-way Darlington Transistor Driver on breakoutboard
  SparkFun Pro Micro: The Pro Micro is similar to the Pro Mini except with an ATmega32U4 on board. The USB transceiver inside the 32U4 allows us to add USB connectivity on-board and do away with bulky external USB interface. Based on: https://github.com/unorthodox-engineers/unorthodox-arduino/blob/master/Unorthodox/fritzing/parts/Pro%20Micro.fzpz
